# Fritzing sketch ESP32-MicroRobotArm (saved by Fritzing 0.9.3b)
breadboards: 2

parts:
  S1 = Pushbutton [package="[THT]"]
  MOTOR12 = Adafruit Gear-Reduced Stepper Motor (small)
  MOTOR14 = Adafruit Gear-Reduced Stepper Motor (small)
  Pololu_A9 = Pololu A4988 [package=SO16]
  Pololu_A10 = Pololu A4988 [package=SO16]
  Pololu_A11 = Pololu A4988 [package=SO16]
  Pololu_A12 = Pololu A4988 [package=SO16]
  MOTOR24 = Adafruit Gear-Reduced Stepper Motor (small)
  MOTOR25 = Adafruit Gear-Reduced Stepper Motor (small)
  MOTOR26 = Adafruit Gear-Reduced Stepper Motor (small)
  MOTOR27 = Adafruit Gear-Reduced Stepper Motor (small)
  MOTOR28 = Adafruit Gear-Reduced Stepper Motor (small)
  U1 = ESP32S-HiLetgo [part_number=ESP32S-HiLetgo]
  R1 = Resistor [tolerance=±5% resistance=10k package="2010 [SMD]"]
  R2 = Resistor [tolerance=±5% resistance=10k package="2010 [SMD]"]
  R3 = Resistor [tolerance=±5% resistance=10k package="2010 [SMD]"]
  ENCODER1 = Rotary Encoder with Knob

nets:
  VDD: S1.Pin_1, S1.Pin_2, Pololu_A9.MS1, Pololu_A9.VDD, Pololu_A10.MS1, Pololu_A10.VDD, Pololu_A11.MS1, Pololu_A11.VDD, Pololu_A12.MS1, Pololu_A12.VDD, U1.3.3, R2.Pin_0, R3.Pin_0
  N1: S1.Pin_3, S1.Pin_4, U1.GPIO34, R1.Pin_1
  N2: MOTOR12.ORANGE, MOTOR14.PINK, Pololu_A9.1A
  N3: MOTOR12.YELLOW, MOTOR14.YELLOW, Pololu_A9.2B
  N4: MOTOR12.PINK, MOTOR14.ORANGE, Pololu_A9.1B
  N5: MOTOR12.BLUE, MOTOR14.BLUE, Pololu_A9.2A
  N6: Pololu_A9.RESET, Pololu_A9.SLEEP
  N7: Pololu_A9.STEP, U1.GPIO2
  N8: Pololu_A9.DIR, U1.GPIO4
  GND: Pololu_A9.GND#8, Pololu_A10.GND#8, Pololu_A11.GND#8, Pololu_A12.GND#8, U1.GND, R1.Pin_0, ENCODER1.GND, ENCODER1.0V
  N9: Pololu_A10.RESET, Pololu_A10.SLEEP
  N10: Pololu_A10.STEP, U1.GPIO16
  N11: Pololu_A10.DIR, U1.GPIO17
  N12: Pololu_A10.1B, MOTOR25.PINK, MOTOR26.ORANGE
  N13: Pololu_A10.1A, MOTOR25.ORANGE, MOTOR26.PINK
  N14: Pololu_A10.2A, MOTOR25.BLUE, MOTOR26.BLUE
  N15: Pololu_A10.2B, MOTOR25.YELLOW, MOTOR26.YELLOW
  N16: Pololu_A11.RESET, Pololu_A11.SLEEP
  N17: Pololu_A11.STEP, U1.GPIO5
  N18: Pololu_A11.DIR, U1.GPIO18
  N19: Pololu_A11.1B, MOTOR27.PINK, MOTOR28.ORANGE
  N20: Pololu_A11.1A, MOTOR27.ORANGE, MOTOR28.PINK
  N21: Pololu_A11.2A, MOTOR27.BLUE, MOTOR28.BLUE
  N22: Pololu_A11.2B, MOTOR27.YELLOW, MOTOR28.YELLOW
  N23: Pololu_A12.RESET, Pololu_A12.SLEEP
  N24: Pololu_A12.STEP, U1.GPIO19
  N25: Pololu_A12.DIR, U1.GPIO21
  N26: Pololu_A12.1B, MOTOR24.PINK
  N27: Pololu_A12.1A, MOTOR24.ORANGE
  N28: Pololu_A12.2A, MOTOR24.BLUE
  N29: Pololu_A12.2B, MOTOR24.YELLOW
  N30: U1.GPIO32, R3.Pin_1, ENCODER1.A
  N31: U1.GPIO33, R2.Pin_1, ENCODER1.B
  VIN: U1.VIN, ENCODER1.+5V

notes:
  12V
  J 3
  J 2
  J 1
  J 4

custom parts:
  Adafruit Gear-Reduced Stepper Motor (small): Adafruit gear-reduction stepper motor (small)
  ESP32S-HiLetgo: HiLetgo ESP-WROOM-32 ESP32 ESP-32S Development Board 2.4GHz Dual-Mode WiFi + Bluetooth Dual Cores Microcontroller The ESP32 integrated with Antenna switches, RF Balun, power amplifiers, low-noise amplifiers, filters, and management modules, and the entire solution occupies the least area of PCB. 2.4 GHz Wi-Fi plus Bluetooth dual-mode chip, with TSMC Ultra-low power consumption 40nm technology,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
  Rotary Encoder with Knob: Rotary Encoder with 1/4" Shaft and Knob
